# Fritzing sketch hardware (saved by Fritzing 0.7.12b)
breadboards: 2

parts:
  R1 = Resistor [tolerance=±10% resistance=100 package=THT]
  LED3 = LED - 5mm [color="Red (633nm)" package="5 mm [THT]"]
  LED2 = LED - 5mm [color="Green (555nm)" package="5 mm [THT]"]
  Pi1 = Adafruit Pi Cobbler
  Q1 = PNP-Transistor [package="TO92 [THT]"]
  LED1 = LED - 5mm [color="Red (633nm)" package="5 mm [THT]"]
  LED5 = LED - 5mm [color="Red (633nm)" package="5 mm [THT]"]
  LED7 = LED - 5mm [color="Red (633nm)" package="5 mm [THT]"]
  LED4 = LED - 5mm [color="Green (555nm)" package="5 mm [THT]"]
  LED6 = LED - 5mm [color="Green (555nm)" package="5 mm [THT]"]
  LED8 = LED - 5mm [color="Green (555nm)" package="5 mm [THT]"]
  R2 = Resistor [tolerance=±10% resistance=100 package=THT]
  Q2 = PNP-Transistor [package="TO92 [THT]"]
  LED10 = LED - 5mm [color="Green (555nm)" package="5 mm [THT]"]
  LED11 = LED - 5mm [color="Red (633nm)" package="5 mm [THT]"]
  LED15 = LED - 5mm [color="Red (633nm)" package="5 mm [THT]"]
  LED13 = LED - 5mm [color="Red (633nm)" package="5 mm [THT]"]
  LED9 = LED - 5mm [color="Red (633nm)" package="5 mm [THT]"]
  LED12 = LED - 5mm [color="Green (555nm)" package="5 mm [THT]"]
  LED14 = LED - 5mm [color="Green (555nm)" package="5 mm [THT]"]
  LED16 = LED - 5mm [color="Green (555nm)" package="5 mm [THT]"]
  LED17 = LED - 5mm [color="Red (633nm)" package="5 mm [THT]"]
  LED23 = LED - 5mm [color="Red (633nm)" package="5 mm [THT]"]
  LED21 = LED - 5mm [color="Red (633nm)" package="5 mm [THT]"]
  LED20 = LED - 5mm [color="Green (555nm)" package="5 mm [THT]"]
  LED22 = LED - 5mm [color="Green (555nm)" package="5 mm [THT]"]
  LED24 = LED - 5mm [color="Green (555nm)" package="5 mm [THT]"]
  R3 = Resistor [tolerance=±10% resistance=100 package=THT]
  Q3 = PNP-Transistor [package="TO92 [THT]"]
  LED18 = LED - 5mm [color="Green (555nm)" package="5 mm [THT]"]
  LED19 = LED - 5mm [color="Red (633nm)" package="5 mm [THT]"]
  J1 = screw terminal, 5 pins
  LCD1 = LCD screen  # not connected
  U1 = 74HC595 [package="DIP16 [THT]"]

nets:
  N1: R1.Pin_0, Q1.C
  N2: R1.Pin_1, LED3.anode, LED2.anode, LED1.anode, LED5.anode, LED7.anode, LED4.anode, LED6.anode, LED8.anode
  N3: LED3.cathode, LED11.cathode, LED19.cathode, U1.Q2
  N4: LED2.cathode, LED10.cathode, LED18.cathode, U1.Q1
  N5: Pi1.5V0, Pi1.PIN4, J1.pin2, U1.VCC
  GND: Pi1.GND, J1.pin1, U1.GND, U1.OE
  N6: Pi1.#17, U1.DS
  N7: Pi1.#21, U1.ST_CP
  N8: Pi1.#22, U1.SH_CP
  N9: Pi1.#23, Q1.B
  N10: Pi1.#24, Q2.B
  N11: Pi1.MOSI, J1.pin4
  N12: Pi1.#25, Q3.B
  N13: Pi1.SCLK, J1.pin3
  N14: Pi1.CE1, J1.pin5
  N15: Q1.E, Q2.E, Q3.E, U1.MR
  N16: LED1.cathode, LED9.cathode, LED17.cathode, U1.Q0
  N17: LED5.cathode, LED13.cathode, LED21.cathode, U1.Q4
  N18: LED7.cathode, LED15.cathode, LED23.cathode, U1.Q6
  N19: LED4.cathode, LED12.cathode, LED20.cathode, U1.Q3
  N20: LED6.cathode, LED14.cathode, LED22.cathode, U1.Q5
  N21: LED8.cathode, LED16.cathode, LED24.cathode, U1.Q7
  N22: R2.Pin_0, Q2.C
  N23: R2.Pin_1, LED10.anode, LED11.anode, LED15.anode, LED13.anode, LED9.anode, LED12.anode, LED14.anode, LED16.anode
  N24: LED17.anode, LED23.anode, LED21.anode, LED20.anode, LED22.anode, LED24.anode, R3.Pin_1, LED18.anode, LED19.anode
  N25: R3.Pin_0, Q3.C

notes:
  LCD connected through Adafruit's LCD I2C/SPI Backpack (not shown here)
  Terminals represent output of Adafruit's LCD I2C/SPI Backpack

custom parts:
  Adafruit Pi Cobbler: Adafruit Pi Cobbler GPIO Breakout for Raspberry Pi
